# Fritzing sketch DisenoFinal (saved by Fritzing 0.9.9b)
perfboards: 1

parts:
  J1 = Terminal Block - 2 pins [package=THT]
  J2 = Terminal Block - 2 pins [package=THT]
  J3 = Terminal Block - 2 pins [package=THT]
  J4 = Terminal Block - 2 pins [package=THT]
  J5 = Terminal Block - 2 pins [package=THT]
  J6 = Terminal Block - 2 pins [package=THT]
  J7 = Terminal Block - 2 pins [package=THT]
  J8 = Terminal Block - 2 pins [package=THT]
  J9 = Terminal Block - 2 pins [package=THT]
  J10 = female pin header, 20 pins [form="♀ (female)"]
  J11 = female pin header, 20 pins [form="♀ (female)"]
  Mod1 = Raspberry Pi Pico W
  R1 = Resistor [tolerance=±5% power=0.25 resistance=4.7k package=THT]  # not connected
  R2 = Resistor [tolerance=±5% power=0.25 resistance=2.2 package=THT]
  R3 = Resistor [tolerance=±5% power=0.25 resistance=4.7k package=THT]
  J12 = RJ11 Jack [package=rj11-6]
  J13 = RJ11 Jack [package=rj11-6]
  Componente1 = MQ-4
  Componente2 = Adafruit LTR390 UV Light Sensor [part_number="Adafruit #4831"]
  Componente3 = Adafruit BME280 [part_number="Adafruit #2652"]

nets:
  N1: J1.Line_1, J10.pin20, Mod1.pin_1, Componente3.SDI/SDA
  N2: J1.Line_2, J10.pin19, Mod1.pin_2, Componente3.SCK/SCL
  N3: J2.Line_1, J10.pin17, Mod1.pin_4, Componente2.SDA
  N4: J2.Line_2, J10.pin16, Mod1.pin_5, Componente2.SCL
  GND: J3.Line_1, J3.Line_2, J5.Line_2, J10.pin3, J10.pin8, J10.pin13, J10.pin18, J11.pin3, J11.pin8, J11.pin13, J11.pin18, Mod1.pin_3, Mod1.pin_8, Mod1.pin_13, Mod1.pin_18, Mod1.pin_23, Mod1.pin_28, Mod1.pin_33, Mod1.pin_38, R2.Pin_1, R3.Pin_1, Componente1.GND, Componente2.GND, Componente3.GND
  VCC: J4.Line_1, J4.Line_2, Componente2.VCC, Componente3.VCC
  N5: J5.Line_1, Componente1.VCC
  N6: J6.Line_1, J11.pin16, Mod1.pin_36, J13.2
  N7: J6.Line_2, J11.pin12, Mod1.pin_32, Componente1.AO
  N8: J7.Line_1, J12.5
  N9: J7.Line_2, J13.3
  N10: J8.Line_1, J11.pin9, Mod1.pin_29, J13.5
  N11: J8.Line_2, J11.pin11, Mod1.pin_31, J13.4
  N12: J9.Line_2, J11.pin7, Mod1.pin_27, J12.2
  N13: J10.pin1, Mod1.pin_20
  N14: J10.pin2, Mod1.pin_19
  N15: J10.pin4, Mod1.pin_17
  N16: J10.pin5, Mod1.pin_16
  N17: J10.pin6, Mod1.pin_15
  N18: J10.pin7, Mod1.pin_14
  N19: J10.pin9, Mod1.pin_12
  N20: J10.pin10, Mod1.pin_11
  N21: J10.pin11, Mod1.pin_10
  N22: J10.pin12, Mod1.pin_9
  N23: J10.pin14, Mod1.pin_7
  N24: J10.pin15, Mod1.pin_6
  N25: J11.pin1, Mod1.pin_21
  N26: J11.pin2, Mod1.pin_22
  N27: J11.pin4, Mod1.pin_24
  N28: J11.pin5, Mod1.pin_25
  N29: J11.pin6, Mod1.pin_26
  N30: J11.pin10, Mod1.pin_30
  N31: J11.pin14, Mod1.pin_34
  N32: J11.pin15, Mod1.pin_35
  N33: J11.pin17, Mod1.pin_37
  N34: J11.pin19, Mod1.pin_39
  N35: J11.pin20, Mod1.pin_40

notes:
  Anemómetro y veleta
  Pluviómetro
  MQ-135

custom parts:
  Terminal Block - 2 pins: Generic Screw Terminal 9.5mm
  Raspberry Pi Pico W: Raspberry Pi Pico W. Based around the RP2040 microcontroller the Pico W is a low cost microcontroller device bringing Raspberry Pi quality, cost, and easy of use to the microcontroller space. The areas marked KEEPOUT in pcb silkscreen should not have traces running through them to avoid shorts on a soldered in module!
  Adafruit LTR390 UV Light Sensor: The LTR390 is one of the few low-cost UV sensors available, and it's a pretty nice one! With both ambient light and UVA sensing with a peak spectral response between 300 and 350nm. You can use it for measuring how much sun you can get before needing to covering up. Unlike the Si1145, this sensor will not give you UV Index readings. However, the Si1145 does UV Index approximations based on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
  Adafruit BME280: Bosch has stepped up their game with their new BME280 sensor, an environmental sensor with temperature, barometric pressure and humidity! This sensor is great for all sorts of indoor environmental sensing and can even be used in both I2C and SPI! This precision sensor from Bosch is the best low-cost sensing solution for measuring humidity with ±3% accuracy, barometric pressure with ±1 hPa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
